// Logisim project s-mips.circ as structural Verilog: 11 circuits, main circuit S-MIPS Board
module S_MIPS_Board (
  input  DESHABILITAR_DISPATCHER,
  output halt
);

  wire button_1_out, CLK, CS, d_ff_1_q, LCLR, LoadRAM, LoadRAMOn, LW, R_R_W, R_W, ram_dispatcher_1_finished,
       RCS, Reset_out, RST, TTY_EN;
  wire [2:0] KDB;
  wire [3:0] LMask, Mask, ram_1_read_time, ram_1_write_time, RMask;
  wire [6:0] KDB_DATA, TTY_DATA;
  wire [15:0] Addr, LAddr, RAddr;
  wire [31:0] I0, I1, I2, I3, LData, ram_1_data_out_0, ram_1_data_out_1, ram_1_data_out_2, ram_1_data_out_3,
       RI0, RI1, RI2, RI3;

  TTY #(.rows(25), .cols(80)) tty_1 (.data(TTY_DATA), .clk(CLK), .we(TTY_EN), .clr(RST));
  not not_1 (LoadRAMOn, ram_dispatcher_1_finished);
  RAM_Dispatcher ram_dispatcher_1 (
    .WriteTime(ram_1_write_time), .Clock(CLK), .Data(LData), .Address(LAddr), .Mask(LMask),
    .Finished(ram_dispatcher_1_finished), .Write(LW), .CLR(LCLR));
  Keyboard #(.buflen(64)) keyboard_1 (.clk(CLK), .re(KDB[0]), .avail(KDB[2]), .data(KDB_DATA));  // open: clr
  RAM ram_1 (
    .Address(RAddr), .Data_Out_0(ram_1_data_out_0), .Data_Out_1(ram_1_data_out_1),
    .Data_Out_2(ram_1_data_out_2), .Data_Out_3(ram_1_data_out_3), .Data_In_0(RI0), .Data_In_1(RI1),
    .Data_In_2(RI2), .Data_In_3(RI3), .Mask(RMask), .nRead_Write(R_R_W), .Chip_Select(RCS),
    .Read_Time(ram_1_read_time), .Reset(button_1_out), .Write_Time(ram_1_write_time));
  Button button_1 (.out(button_1_out));
  D_Flip_Flop d_ff_1 (.clk(CLK), .D(1'b1), .Q(d_ff_1_q), .reset(Reset_out));  // open: Qn, preset, en
  Button Reset (.out(Reset_out));
  S_MIPS s_mips_1 (
    .Kbd_Enable(KDB[0]), .Address(Addr), .Kbd_Clear(KDB[1]), .Kbd_Available(KDB[2]), .RAM_In_0(I0),
    .Kbd_ASCII_Data(KDB_DATA), .RAM_In_1(I1), .TTY_Enable(TTY_EN), .RAM_In_2(I2), .RAM_In_3(I3),
    .TTY_ASCII_Data(TTY_DATA), .Reset(RST), .RAM_Out_0(ram_1_data_out_0), .Clock(CLK),
    .RAM_Out_1(ram_1_data_out_1), .Stop(halt), .RAM_Out_2(ram_1_data_out_2), .RAM_Out_3(ram_1_data_out_3),
    .Mask(Mask), .Read_Time(ram_1_read_time), .Write_Time(ram_1_write_time), .nRead_Write(R_W),
    .Chip_Select(CS));
  D_Flip_Flop d_ff_2 (.clk(CLK), .D(d_ff_1_q), .Qn(LCLR), .reset(Reset_out));  // open: Q, preset, en
  or or_1 (RST, LCLR, LoadRAM);
  Clock clock_1 (.out(CLK));
  Multiplexer #(.width(32), .enable("false")) multiplexer_1 (.in0(I0), .in1(LData), .out(RI0), .sel(LoadRAM));
  Multiplexer #(.width(32), .enable("false")) multiplexer_2 (.in0(I1), .in1(LData), .out(RI1), .sel(LoadRAM));
  Multiplexer #(.width(32), .enable("false")) multiplexer_3 (.in0(I2), .in1(LData), .out(RI2), .sel(LoadRAM));
  Multiplexer #(.width(32), .enable("false")) multiplexer_4 (.in0(I3), .in1(LData), .out(RI3), .sel(LoadRAM));
  and and_1 (LoadRAM, ~DESHABILITAR_DISPATCHER, LoadRAMOn);  // AND_Gate
  Multiplexer #(.width(16), .enable("false")) multiplexer_5 (.in0(Addr), .in1(LAddr), .out(RAddr), .sel(LoadRAM));
  Multiplexer #(.width(4), .enable("false")) multiplexer_6 (.in0(Mask), .in1(LMask), .out(RMask), .sel(LoadRAM));
  Multiplexer #(.enable("false")) multiplexer_7 (.in0(CS), .in1(LW), .out(RCS), .sel(LoadRAM));
  Multiplexer #(.enable("false")) multiplexer_8 (.in0(R_W), .in1(LW), .out(R_R_W), .sel(LoadRAM));

  // Notes on the sheet:
  //   NO MODIFICAR
  //   Keyboard
endmodule

module RAM (
  input  [15:0] Address,
  input  [31:0] Data_In_0,
  input  [31:0] Data_In_1,
  input  [31:0] Data_In_2,
  input  [31:0] Data_In_3,
  input  [3:0] Mask,
  input  nRead_Write,
  input  Chip_Select,
  input  Reset,
  output [31:0] Data_Out_0,
  output [31:0] Data_Out_1,
  output [31:0] Data_Out_2,
  output [31:0] Data_Out_3,
  output [3:0] Read_Time,
  output [3:0] Write_Time
);

  wire and_2_out, and_3_out, and_4_out, and_5_out, and_6_out, and_7_out, and_8_out, and_9_out, Changed, CLK,
       comparator_2_eq, comparator_3_eq, comparator_4_eq, comparator_5_eq, comparator_6_eq, Count,
       demultiplexer_3_out0, Idle, Idle_q, Load, Load0, Load1, nand_1_out, or_1_out, or_2_out, or_3_out,
       or_4_out, or_5_out, or_6_out, or_7_out, or_8_out, or_9_out, or_10_out, Proc_q, Update_Mem, Zero_Time;
  wire [3:0] counter_1_q, multiplexer_1_out, subtractor_1_out;
  wire [31:0] register_1_q, register_2_q, register_3_q, register_4_q, register_5_q;

  // Probe on 4'b0011
  // Probe on 4'b0010
  Multiplexer #(.width(4), .enable("false")) multiplexer_1 (
    .in0(4'b0011), .in1(4'b0010), .out(multiplexer_1_out), .sel(nRead_Write));
  or or_1 (or_1_out, Idle, Update_Mem);
  or or_2 (or_2_out, ~Chip_Select, Reset);  // OR_Gate
  Subtractor #(.width(4)) subtractor_1 (.a(multiplexer_1_out), .b(4'b0010), .out(subtractor_1_out));  // open: bin, bout
  Demultiplexer #(.enable("false")) demultiplexer_1 (.out0(Idle), .out1(Load0), .in(Idle_q), .sel(Changed));
  D_Flip_Flop u_Idle (.clk(CLK), .D(or_1_out), .Q(Idle_q), .preset(or_2_out));  // open: Qn, en, reset
  // Probe on counter_1_q
  Counter #(.width(4), .max('hf)) counter_1 (
    .load(Load), .D(subtractor_1_out), .count(Count), .Q(counter_1_q), .clk(CLK), .clr(or_3_out));  // open: carry
  or or_3 (or_3_out, ~Chip_Select, Reset);  // OR_Gate
  Comparator #(.width(4), .mode("unsigned")) comparator_1 (
    .a(4'b0000), .b(counter_1_q), .eq(Zero_Time));  // open: gt, lt
  or or_4 (or_4_out, Count, Load0, Load1);
  Register #(.width(32)) register_1 (.D(Data_In_0), .en(Chip_Select), .Q(register_1_q), .clk(CLK), .clr(or_5_out));
  or or_5 (or_5_out, ~Chip_Select, Reset);  // OR_Gate
  Register #(.width(32)) register_2 (.D(Data_In_1), .en(Chip_Select), .Q(register_2_q), .clk(CLK), .clr(or_6_out));
  or or_6 (or_6_out, ~Chip_Select, Reset);  // OR_Gate
  Register #(.width(32)) register_3 (.D(Data_In_2), .en(Chip_Select), .Q(register_3_q), .clk(CLK), .clr(or_7_out));
  or or_7 (or_7_out, ~Chip_Select, Reset);  // OR_Gate
  Register #(.width(32)) register_4 (.D(Data_In_3), .en(Chip_Select), .Q(register_4_q), .clk(CLK), .clr(or_8_out));
  or or_8 (or_8_out, ~Chip_Select, Reset);  // OR_Gate
  Register #(.width(32)) register_5 (
    .D({{11{1'b1}}, nRead_Write, Mask, Address}), .en(Chip_Select), .Q(register_5_q), .clk(CLK),
    .clr(or_9_out));
  or or_9 (or_9_out, ~Chip_Select, Reset);  // OR_Gate
  D_Flip_Flop Proc (.clk(CLK), .D(or_4_out), .Q(Proc_q), .reset(or_10_out));  // open: Qn, preset, en
  or or_10 (or_10_out, ~Chip_Select, Reset);  // OR_Gate
  Demultiplexer #(.enable("false")) demultiplexer_2 (
    .out0(Count), .out1(Update_Mem), .in(demultiplexer_3_out0), .sel(Zero_Time));
  Demultiplexer #(.enable("false")) demultiplexer_3 (
    .out0(demultiplexer_3_out0), .out1(Load1), .in(Proc_q), .sel(Changed));
  Clock clock_1 (.out(CLK));
  Comparator #(.width(32)) comparator_2 (.a(register_1_q), .b(Data_In_0), .eq(comparator_2_eq));  // open: gt, lt
  Comparator #(.width(32)) comparator_3 (.a(register_2_q), .b(Data_In_1), .eq(comparator_3_eq));  // open: gt, lt
  Comparator #(.width(32)) comparator_4 (.a(register_3_q), .b(Data_In_2), .eq(comparator_4_eq));  // open: gt, lt
  Comparator #(.width(32)) comparator_5 (.a(register_4_q), .b(Data_In_3), .eq(comparator_5_eq));  // open: gt, lt
  Comparator #(.width(32)) comparator_6 (
    .a(register_5_q), .b({{11{1'b1}}, nRead_Write, Mask, Address}), .eq(comparator_6_eq));  // open: gt, lt
  nand nand_1 (nand_1_out, comparator_6_eq, comparator_2_eq, comparator_3_eq, comparator_4_eq, comparator_5_eq);
  and and_1 (Changed, nand_1_out, Chip_Select);
  or or_11 (Load, Count, Load1, Load0);
  and and_2 (and_2_out, Mask[0], Update_Mem, nRead_Write);
  and and_3 (and_3_out, Mask[1], Update_Mem, nRead_Write);
  and and_4 (and_4_out, Mask[2], Update_Mem, nRead_Write);
  and and_5 (and_5_out, Mask[3], Update_Mem, nRead_Write);
  RAM_part #(.addrWidth(16), .dataWidth(32), .bus("separate")) ram_1 (
    .addr(Address), .din(Data_In_0), .data(Data_Out_0), .str(and_2_out), .sel(Chip_Select), .clk(CLK),
    .ld(and_6_out), .clr(Reset));
  and and_6 (and_6_out, ~nRead_Write, Idle);  // AND_Gate
  RAM_part #(.addrWidth(16), .dataWidth(32), .bus("separate")) ram_2 (
    .addr(Address), .din(Data_In_1), .data(Data_Out_1), .str(and_3_out), .sel(Chip_Select), .clk(CLK),
    .ld(and_7_out), .clr(Reset));
  and and_7 (and_7_out, ~nRead_Write, Idle);  // AND_Gate
  RAM_part #(.addrWidth(16), .dataWidth(32), .bus("separate")) ram_3 (
    .addr(Address), .din(Data_In_2), .data(Data_Out_2), .str(and_4_out), .sel(Chip_Select), .clk(CLK),
    .ld(and_8_out), .clr(Reset));
  and and_8 (and_8_out, ~nRead_Write, Idle);  // AND_Gate
  RAM_part #(.addrWidth(16), .dataWidth(32), .bus("separate")) ram_4 (
    .addr(Address), .din(Data_In_3), .data(Data_Out_3), .str(and_5_out), .sel(Chip_Select), .clk(CLK),
    .ld(and_9_out), .clr(Reset));
  and and_9 (and_9_out, ~nRead_Write, Idle);  // AND_Gate

  assign Read_Time = 4'b0011;
  assign Write_Time = 4'b0010;

  // Other names for the same wires on the sheet: M0 = Mask[0]; M1 = Mask[1]; M2 = Mask[2]; M3 = Mask[3];
  //   RW = nRead_Write; CLR = Reset; CS = Chip_Select; Load2 = Count

  // Notes on the sheet:
  //   NO MODIFICAR
  //   excepto quizás los valores RT y WT
  //   BANK0
  //   BANK1
  //   BANK2
  //   BANK3
endmodule

module S_MIPS (
  input  Kbd_Available,
  input  [6:0] Kbd_ASCII_Data,
  input  [31:0] RAM_Out_0,
  input  [31:0] RAM_Out_1,
  input  Reset,
  input  [31:0] RAM_Out_2,
  input  Clock,
  input  [31:0] RAM_Out_3,
  input  [3:0] Read_Time,
  input  [3:0] Write_Time,
  output Kbd_Enable,
  output [15:0] Address,
  output Kbd_Clear,
  output TTY_Enable,
  output [6:0] TTY_ASCII_Data,
  output Stop,
  output [31:0] RAM_In_0,
  output [31:0] RAM_In_1,
  output [31:0] RAM_In_2,
  output [31:0] RAM_In_3,
  output [3:0] Mask,
  output nRead_Write,
  output Chip_Select
);


  // Other names for the same wires on the sheet: CLK = Clock; CLR = Reset; CS = Chip_Select;
  //   KBD_AVAIL = Kbd_Available; KBD_CLR = Kbd_Clear; KBD_DATA[6:0] = Kbd_ASCII_Data; RAM_A[15:0] = Address;
  //   RAM_INPUT_0[31:0] = RAM_In_0; RAM_INPUT_1[31:0] = RAM_In_1; RAM_INPUT_2[31:0] = RAM_In_2;
  //   RAM_INPUT_3[31:0] = RAM_In_3; RAM_MASK[3:0] = Mask; RAM_OUTPUT_0[31:0] = RAM_Out_0;
  //   RAM_OUTPUT_1[31:0] = RAM_Out_1; RAM_OUTPUT_2[31:0] = RAM_Out_2; RAM_OUTPUT_3[31:0] = RAM_Out_3;
  //   RW = nRead_Write; TTY_DATA[6:0] = TTY_ASCII_Data

  // Notes on the sheet:
  //   RAM ADDRESS
  //   DATA FROM RAM
  //   DATA TO RAM
  //   DATA WRITE MASK
  //   RAM TIMING
  //   RAM CONTROL
  //   KEYBOARD
  //   TTY
  //   SEQUENCING
endmodule

module RAM_Dispatcher (
  input  [3:0] WriteTime,
  input  Clock,
  input  CLR,
  output [31:0] Data,
  output [15:0] Address,
  output [3:0] Mask,
  output Finished,
  output Write
);

  wire demultiplexer_2_out1, demultiplexer_3_out1, End, IDLE_q, IncAddr, Load, or_1_out, or_2_out, While_q,
       WriteEnd;
  wire [3:0] counter_1_q;
  wire [31:0] CurrentAddress_q;

  Counter #(.width(32), .max('hffffffff)) CurrentAddress (
    .count(IncAddr), .Q({CurrentAddress_q[31:18], Address, CurrentAddress_q[1:0]}), .clk(Clock), .clr(CLR));  // open: load, D, carry
  or or_1 (or_1_out, IncAddr, demultiplexer_3_out1, Finished);
  D_Flip_Flop IDLE (.clk(Clock), .D(or_1_out), .Q(IDLE_q), .preset(CLR));  // open: Qn, en, reset
  Demultiplexer #(.enable("false")) demultiplexer_1 (.out0(Load), .out1(Finished), .in(IDLE_q), .sel(End));
  D_Flip_Flop While (.clk(Clock), .D(or_2_out), .Q(While_q), .reset(CLR));  // open: Qn, preset, en
  or or_2 (or_2_out, Write, Load);
  RAM_part #(.addrWidth(18), .dataWidth(32)) ram_1 (
    .addr({Address, CurrentAddress_q[1:0]}), .data(Data), .clk(Clock));  // open: sel, ld, clr
  Demultiplexer #(.enable("false")) demultiplexer_2 (
    .out0(Write), .out1(demultiplexer_2_out1), .in(While_q), .sel(WriteEnd));
  Decoder #(.select(2)) decoder_1 (
    .out0(Mask[0]), .out1(Mask[1]), .out2(Mask[2]), .out3(Mask[3]), .sel(CurrentAddress_q[1:0]));  // open: en
  Demultiplexer #(.enable("false")) demultiplexer_3 (
    .out0(IncAddr), .out1(demultiplexer_3_out1), .in(demultiplexer_2_out1), .sel(End));
  Counter #(.width(4), .max('hf)) counter_1 (
    .load(Load), .D(WriteTime), .count(Write), .Q(counter_1_q), .clk(Clock));  // open: carry, clr
  Comparator #(.width(32)) comparator_1 (.a(Data), .b({32{1'b1}}), .eq(End));  // open: gt, lt
  Comparator #(.width(4)) comparator_2 (.a(4'b0000), .b(counter_1_q), .eq(WriteEnd));  // open: gt, lt

  // Other names for the same wires on the sheet: CLK = Clock; Count = Write; WT[3:0] = WriteTime
endmodule

module Register_File (
  input  [4:0] DA,
  input  [31:0] DI,
  input  Clk,
  input  Reset,
  input  R_W,
  input  [4:0] SA,
  input  [4:0] SB,
  input  Mult_or_Div,
  input  [31:0] Hi_Input,
  input  [31:0] Lo_Input,
  output [31:0] A,
  output [31:0] B,
  output [31:0] Stack_Pointer,
  output [31:0] Hi_Output,
  output [31:0] Lo_Output
);

  wire E01, E02, E03, E04, E05, E06, E07, E08, E09, E10, E11, E12, E13, E14, E15, E16, E17, E18, E19, E20,
       E21, E22, E23, E24, E25, E26, E27, E28, E29, E30, E31;
  wire [31:0] D00, D01, D02, D03, D04, D05, D06, D07, D08, D09, D10, D11, D12, D13, D14, D15, D16, D17, D18,
       D19, D20, D21, D22, D23, D24, D25, D26, D27, D28, D29, D30;

  Register #(.width(32)) register_1 (.D(DI), .en(1'b0), .Q(D00), .clk(Clk), .clr(Reset));
  Register #(.width(32)) register_2 (.D(DI), .en(E01), .Q(D01), .clk(Clk), .clr(Reset));
  Register #(.width(32)) register_3 (.D(DI), .en(E02), .Q(D02), .clk(Clk), .clr(Reset));
  Register #(.width(32)) register_4 (.D(DI), .en(E03), .Q(D03), .clk(Clk), .clr(Reset));
  Register #(.width(32)) register_5 (.D(DI), .en(E04), .Q(D04), .clk(Clk), .clr(Reset));
  Register #(.width(32)) register_6 (.D(DI), .en(E05), .Q(D05), .clk(Clk), .clr(Reset));
  Register #(.width(32)) register_7 (.D(DI), .en(E06), .Q(D06), .clk(Clk), .clr(Reset));
  Register #(.width(32)) register_8 (.D(DI), .en(E07), .Q(D07), .clk(Clk), .clr(Reset));
  Register #(.width(32)) register_9 (.D(DI), .en(E08), .Q(D08), .clk(Clk), .clr(Reset));
  Register #(.width(32)) register_10 (.D(DI), .en(E09), .Q(D09), .clk(Clk), .clr(Reset));
  Register #(.width(32)) register_11 (.D(DI), .en(E10), .Q(D10), .clk(Clk), .clr(Reset));
  Register #(.width(32)) register_12 (.D(DI), .en(E11), .Q(D11), .clk(Clk), .clr(Reset));
  Register #(.width(32)) register_13 (.D(DI), .en(E12), .Q(D12), .clk(Clk), .clr(Reset));
  Register #(.width(32)) register_14 (.D(DI), .en(E13), .Q(D13), .clk(Clk), .clr(Reset));
  Register #(.width(32)) register_15 (.D(DI), .en(E14), .Q(D14), .clk(Clk), .clr(Reset));
  Register #(.width(32)) register_16 (.D(DI), .en(E15), .Q(D15), .clk(Clk), .clr(Reset));
  Multiplexer #(.select(5), .width(32), .enable("false")) multiplexer_1 (
    .in0(D00), .in1(D01), .in2(D02), .in3(D03), .in4(D04), .in5(D05), .in6(D06), .in7(D07), .in8(D08),
    .in9(D09), .in10(D10), .in11(D11), .in12(D12), .in13(D13), .in14(D14), .in15(D15), .in16(D16),
    .in17(D17), .in18(D18), .in19(D19), .in20(D20), .in21(D21), .in22(D22), .in23(D23), .in24(D24),
    .in25(D25), .in26(D26), .in27(D27), .in28(D28), .in29(D29), .in30(D30), .in31(Stack_Pointer), .out(A),
    .sel(SA));
  Register #(.width(32)) Hi (.D(Hi_Input), .en(Mult_or_Div), .Q(Hi_Output), .clk(Clk));  // open: clr
  Register #(.width(32)) Lo (.D(Lo_Input), .en(Mult_or_Div), .Q(Lo_Output), .clk(Clk));  // open: clr
  Register #(.width(32)) register_17 (.D(DI), .en(E16), .Q(D16), .clk(Clk), .clr(Reset));
  Register #(.width(32)) register_18 (.D(DI), .en(E17), .Q(D17), .clk(Clk), .clr(Reset));
  Register #(.width(32)) register_19 (.D(DI), .en(E18), .Q(D18), .clk(Clk), .clr(Reset));
  Register #(.width(32)) register_20 (.D(DI), .en(E19), .Q(D19), .clk(Clk), .clr(Reset));
  Register #(.width(32)) register_21 (.D(DI), .en(E20), .Q(D20), .clk(Clk), .clr(Reset));
  Register #(.width(32)) register_22 (.D(DI), .en(E21), .Q(D21), .clk(Clk), .clr(Reset));
  Register #(.width(32)) register_23 (.D(DI), .en(E22), .Q(D22), .clk(Clk), .clr(Reset));
  Register #(.width(32)) register_24 (.D(DI), .en(E23), .Q(D23), .clk(Clk), .clr(Reset));
  Register #(.width(32)) register_25 (.D(DI), .en(E24), .Q(D24), .clk(Clk), .clr(Reset));
  Register #(.width(32)) register_26 (.D(DI), .en(E25), .Q(D25), .clk(Clk), .clr(Reset));
  Register #(.width(32)) register_27 (.D(DI), .en(E26), .Q(D26), .clk(Clk), .clr(Reset));
  Register #(.width(32)) register_28 (.D(DI), .en(E27), .Q(D27), .clk(Clk), .clr(Reset));
  Register #(.width(32)) register_29 (.D(DI), .en(E28), .Q(D28), .clk(Clk), .clr(Reset));
  Register #(.width(32)) register_30 (.D(DI), .en(E29), .Q(D29), .clk(Clk), .clr(Reset));
  Register #(.width(32)) register_31 (.D(DI), .en(E30), .Q(D30), .clk(Clk), .clr(Reset));
  Register #(.width(32)) register_32 (.D(DI), .en(E31), .Q(Stack_Pointer), .clk(Clk), .clr(Reset));
  Multiplexer #(.select(5), .width(32), .enable("false")) multiplexer_2 (
    .in0(D00), .in1(D01), .in2(D02), .in3(D03), .in4(D04), .in5(D05), .in6(D06), .in7(D07), .in8(D08),
    .in9(D09), .in10(D10), .in11(D11), .in12(D12), .in13(D13), .in14(D14), .in15(D15), .in16(D16),
    .in17(D17), .in18(D18), .in19(D19), .in20(D20), .in21(D21), .in22(D22), .in23(D23), .in24(D24),
    .in25(D25), .in26(D26), .in27(D27), .in28(D28), .in29(D29), .in30(D30), .in31(Stack_Pointer), .out(B),
    .sel(SB));
  Demultiplexer #(.select(5), .enable("false")) demultiplexer_1 (
    .out1(E01), .out2(E02), .out3(E03), .out4(E04), .out5(E05), .out6(E06), .out7(E07), .out8(E08),
    .out9(E09), .out10(E10), .out11(E11), .out12(E12), .out13(E13), .out14(E14), .out15(E15), .out16(E16),
    .out17(E17), .out18(E18), .out19(E19), .out20(E20), .out21(E21), .out22(E22), .out23(E23), .out24(E24),
    .out25(E25), .out26(E26), .out27(E27), .out28(E28), .out29(E29), .out30(E30), .out31(E31), .in(R_W),
    .sel(DA));  // open: out0

  // Other names for the same wires on the sheet: C = Clk; D31[31:0] = Stack_Pointer; IN[31:0] = DI; R = Reset;
  //   WRITE = R_W

  // Notes on the sheet:
  //   Inputs
  //   Register File
  //   Outputs
endmodule

module Multiplication (
  input  [31:0] A,
  input  [31:0] B,
  output [31:0] HI,
  output [31:0] LO
);

  wire [31:0] multiplexer_1_out, multiplexer_2_out, negator_1_out, negator_2_out;

  Negator #(.width(32)) negator_1 (.in(A), .out(negator_1_out));
  Negator #(.width(32)) negator_2 (.in(B), .out(negator_2_out));
  // Probe on multiplexer_1_out
  Multiplexer #(.width(32), .enable("false")) multiplexer_1 (
    .in0(A), .in1(negator_1_out), .out(multiplexer_1_out), .sel(A[31]));
  Multiplexer #(.width(32), .enable("false")) multiplexer_2 (
    .in0(B), .in1(negator_2_out), .out(multiplexer_2_out), .sel(B[31]));
  // Probe on multiplexer_2_out
  Multiplier #(.width(32)) multiplier_1 (
    .a(multiplexer_1_out), .b(multiplexer_2_out), .out(LO), .cout(HI));  // open: cin

  // Notes on the sheet:
  //   Unsigned_Multiplication
endmodule

module Division (
  input  [31:0] A,
  input  [31:0] B,
  output [31:0] HI,
  output [31:0] LO
);

  wire [31:0] multiplexer_1_out, multiplexer_2_out, negator_1_out, negator_2_out;

  // Probe on B
  // Probe on A
  Negator #(.width(32)) negator_1 (.in(A), .out(negator_1_out));
  Negator #(.width(32)) negator_2 (.in(B), .out(negator_2_out));
  Multiplexer #(.width(32), .enable("false")) multiplexer_1 (
    .in0(A), .in1(negator_1_out), .out(multiplexer_1_out), .sel(A[31]));
  Multiplexer #(.width(32), .enable("false")) multiplexer_2 (
    .in0(B), .in1(negator_2_out), .out(multiplexer_2_out), .sel(B[31]));
  // Probe on multiplexer_1_out
  Divider #(.width(32)) divider_1 (.a(multiplexer_1_out), .b(multiplexer_2_out), .out(LO), .rem(HI));  // open: upper
  // Probe on multiplexer_2_out
  // Probe on HI

  // Notes on the sheet:
  //   Unsigned_Division
endmodule

module ALU (
  input  [31:0] Operator_A,
  input  [31:0] Operator_B,
  input  [3:0] Selector,
  output [31:0] Output,
  output Zero,
  output Neg
);

  wire [31:0] ADD, AND, DIV, HI, LO, MUL, NOR, OR, REM, SUB, XOR;

  assign AND = Operator_A & Operator_B;  // AND_Gate and_1, 32 bits wide
  assign OR = Operator_A | Operator_B;  // OR_Gate or_1, 32 bits wide
  assign NOR = ~(Operator_A | Operator_B);  // NOR_Gate nor_1, 32 bits wide
  assign XOR = Operator_A ^ Operator_B;  // XOR_Gate xor_1, 32 bits wide
  // Probe on Operator_A
  // Probe on Operator_B
  Adder #(.width(32)) adder_1 (.a(Operator_A), .b(Operator_B), .out(ADD));  // open: cin, cout
  Subtractor #(.width(32)) subtractor_1 (.a(Operator_A), .b(Operator_B), .out(SUB));  // open: bin, bout
  // Probe on MUL
  Multiplier #(.width(32)) multiplier_1 (.a(Operator_A), .b(Operator_B), .out(MUL));  // open: cin, cout
  Divider #(.width(32)) divider_1 (.a(Operator_A), .b(Operator_B), .out(DIV), .rem(REM));  // open: upper
  // Probe on DIV
  Multiplexer #(.select(4), .width(32), .enable("false")) multiplexer_1 (
    .in0(AND), .in1(OR), .in2(NOR), .in3(XOR), .in4(ADD), .in5(SUB), .in6(MUL), .in7(DIV), .in8(REM),
    .out(Output), .sel(Selector));  // open: in9, in10, in11, in12, in13, in14, in15
  Multiplication multiplication_1 (.A(Operator_A), .B(Operator_B), .HI(HI), .LO(LO));
  Division division_1 (.A(Operator_A), .B(Operator_B), .HI(HI), .LO(LO));
  // Probe on Output
  Comparator #(.width(32)) comparator_1 (.a(Output), .b({32{1'b0}}), .eq(Zero), .lt(Neg));  // open: gt

  // Other names for the same wires on the sheet: A[31:0] = Operator_A; B[31:0] = Operator_B; Selec[3:0] = Selector

  // Notes on the sheet:
  //   Inputs
  //   ALU
  //   FLAGS
endmodule

module Instruction_Decoder (
  input  [31:0] Instruction,
  output ADD,
  output AND,
  output SLT,
  output NOP,
  output LW,
  output SUB,
  output OR,
  output SLTU,
  output BEQ,
  output SW,
  output MULT,
  output NOR,
  output SLTI,
  output BNE,
  output POP,
  output MULU,
  output XOR,
  output SLTIU,
  output BLEZ,
  output PUSH,
  output DIV,
  output ANDI,
  output BGTZ,
  output DIVU,
  output ORI,
  output MFHI,
  output BLTZ,
  output HALT,
  output ADDI,
  output XORI,
  output MFLO,
  output J,
  output TTY,
  output JR,
  output RND,
  output KBD
);

  wire _000000, _001010, _001100, _111111, comparator_11_eq, comparator_11_gt, comparator_12_eq,
       comparator_16_eq, comparator_17_eq, comparator_18_eq, comparator_19_eq, comparator_20_eq,
       comparator_21_eq, comparator_22_eq, comparator_23_eq, comparator_24_eq, comparator_25_eq,
       comparator_26_eq, comparator_27_eq, comparator_28_eq, comparator_29_eq, comparator_30_eq,
       comparator_31_eq, comparator_32_eq, comparator_33_eq, comparator_34_eq, comparator_35_eq,
       comparator_36_eq, comparator_37_eq, comparator_38_eq, not_1_out, not_2_out, not_3_out;

  Comparator #(.width(6)) comparator_1 (.a(Instruction[31:26]), .b({6{1'b0}}), .eq(_000000));  // open: gt, lt
  Comparator #(.width(6)) comparator_2 (.a(Instruction[31:26]), .b({6{1'b1}}), .eq(_111111));  // open: gt, lt
  Comparator #(.width(6)) comparator_3 (.a(Instruction[31:26]), .b(6'b001000), .eq(ADDI));  // open: gt, lt
  Comparator #(.width(6)) comparator_4 (.a(Instruction[31:26]), .b(6'b001010), .eq(_001010));  // open: gt, lt
  Comparator #(.width(6)) comparator_5 (.a(Instruction[31:26]), .b(6'b000100), .eq(BEQ));  // open: gt, lt
  Comparator #(.width(6)) comparator_6 (.a(Instruction[31:26]), .b(6'b001100), .eq(_001100));  // open: gt, lt
  Comparator #(.width(6)) comparator_7 (.a(Instruction[31:26]), .b(6'b000101), .eq(BNE));  // open: gt, lt
  Comparator #(.width(6)) comparator_8 (.a(Instruction[31:26]), .b(6'b000110), .eq(BLEZ));  // open: gt, lt
  Comparator #(.width(6)) comparator_9 (.a(Instruction[31:26]), .b(6'b100011), .eq(LW));  // open: gt, lt
  Comparator #(.width(6)) comparator_10 (.a(Instruction[31:26]), .b(6'b101011), .eq(SW));  // open: gt, lt
  Comparator #(.width(6)) comparator_11 (
    .a(Instruction[5:0]), .b({6{1'b0}}), .gt(comparator_11_gt), .eq(comparator_11_eq));  // open: lt
  Comparator #(.width(6)) comparator_12 (.a(Instruction[31:26]), .b(6'b111000), .eq(comparator_12_eq));  // open: gt, lt
  Comparator #(.width(6)) comparator_13 (.a(Instruction[31:26]), .b(6'b000001), .eq(BLTZ));  // open: gt, lt
  Comparator #(.width(6)) comparator_14 (.a(Instruction[31:26]), .b(6'b000010), .eq(J));  // open: gt, lt
  Comparator #(.width(6)) comparator_15 (.a(Instruction[31:26]), .b(6'b000111), .eq(BGTZ));  // open: gt, lt
  and and_1 (POP, comparator_11_eq, comparator_12_eq);
  and and_2 (PUSH, comparator_11_gt, comparator_12_eq);
  Comparator #(.width(6)) comparator_16 (.a(Instruction[5:0]), .b(6'b001011), .eq(comparator_16_eq));  // open: gt, lt
  and and_3 (SLTIU, _001100, comparator_16_eq);
  not not_1 (not_1_out, SLTIU);
  and and_4 (SLTI, not_1_out, _001100);
  Comparator #(.width(6)) comparator_17 (.a(Instruction[5:0]), .b({6{1'b1}}), .eq(comparator_17_eq));  // open: gt, lt
  Comparator #(.width(6)) comparator_18 (.a(Instruction[5:0]), .b(6'b000001), .eq(comparator_18_eq));  // open: gt, lt
  Comparator #(.width(6)) comparator_19 (.a(Instruction[5:0]), .b(6'b000010), .eq(comparator_19_eq));  // open: gt, lt
  Comparator #(.width(6)) comparator_20 (.a(Instruction[5:0]), .b(6'b000100), .eq(comparator_20_eq));  // open: gt, lt
  Comparator #(.width(6)) comparator_21 (.a(Instruction[5:0]), .b(6'b001101), .eq(comparator_21_eq));  // open: gt, lt
  Comparator #(.width(6)) comparator_22 (.a(Instruction[5:0]), .b(6'b001110), .eq(comparator_22_eq));  // open: gt, lt
  and and_5 (HALT, _111111, comparator_17_eq);
  and and_6 (TTY, _111111, comparator_18_eq);
  and and_7 (RND, _111111, comparator_19_eq);
  and and_8 (KBD, _111111, comparator_20_eq);
  and and_9 (ORI, _001010, comparator_21_eq);
  and and_10 (XORI, _001010, comparator_22_eq);
  not not_2 (not_2_out, ORI);
  not not_3 (not_3_out, XORI);
  and and_11 (ANDI, not_2_out, not_3_out, _001010);
  and and_12 (NOP, _000000, comparator_23_eq);
  Comparator #(.width(6)) comparator_23 (.a(Instruction[5:0]), .b({6{1'b0}}), .eq(comparator_23_eq));  // open: gt, lt
  and and_13 (ADD, _000000, comparator_24_eq);
  Comparator #(.width(6)) comparator_24 (.a(Instruction[5:0]), .b(6'b100000), .eq(comparator_24_eq));  // open: gt, lt
  and and_14 (SUB, _000000, comparator_25_eq);
  Comparator #(.width(6)) comparator_25 (.a(Instruction[5:0]), .b(6'b100010), .eq(comparator_25_eq));  // open: gt, lt
  and and_15 (MULT, _000000, comparator_26_eq);
  Comparator #(.width(6)) comparator_26 (.a(Instruction[5:0]), .b(6'b011000), .eq(comparator_26_eq));  // open: gt, lt
  and and_16 (MULU, _000000, comparator_27_eq);
  Comparator #(.width(6)) comparator_27 (.a(Instruction[5:0]), .b(6'b011001), .eq(comparator_27_eq));  // open: gt, lt
  and and_17 (DIV, _000000, comparator_28_eq);
  Comparator #(.width(6)) comparator_28 (.a(Instruction[5:0]), .b(6'b011010), .eq(comparator_28_eq));  // open: gt, lt
  and and_18 (DIVU, _000000, comparator_29_eq);
  Comparator #(.width(6)) comparator_29 (.a(Instruction[5:0]), .b(6'b011011), .eq(comparator_29_eq));  // open: gt, lt
  and and_19 (SLT, _000000, comparator_30_eq);
  Comparator #(.width(6)) comparator_30 (.a(Instruction[5:0]), .b(6'b101010), .eq(comparator_30_eq));  // open: gt, lt
  and and_20 (SLTU, _000000, comparator_31_eq);
  Comparator #(.width(6)) comparator_31 (.a(Instruction[5:0]), .b(6'b101011), .eq(comparator_31_eq));  // open: gt, lt
  and and_21 (AND, _000000, comparator_32_eq);
  Comparator #(.width(6)) comparator_32 (.a(Instruction[5:0]), .b(6'b100100), .eq(comparator_32_eq));  // open: gt, lt
  and and_22 (OR, _000000, comparator_33_eq);
  Comparator #(.width(6)) comparator_33 (.a(Instruction[5:0]), .b(6'b100101), .eq(comparator_33_eq));  // open: gt, lt
  and and_23 (NOR, _000000, comparator_34_eq);
  Comparator #(.width(6)) comparator_34 (.a(Instruction[5:0]), .b(6'b100111), .eq(comparator_34_eq));  // open: gt, lt
  and and_24 (XOR, _000000, comparator_35_eq);
  Comparator #(.width(6)) comparator_35 (.a(Instruction[5:0]), .b(6'b101000), .eq(comparator_35_eq));  // open: gt, lt
  and and_25 (JR, _000000, comparator_36_eq);
  Comparator #(.width(6)) comparator_36 (.a(Instruction[5:0]), .b(6'b001000), .eq(comparator_36_eq));  // open: gt, lt
  and and_26 (MFHI, _000000, comparator_37_eq);
  Comparator #(.width(6)) comparator_37 (.a(Instruction[5:0]), .b(6'b010000), .eq(comparator_37_eq));  // open: gt, lt
  and and_27 (MFLO, _000000, comparator_38_eq);
  Comparator #(.width(6)) comparator_38 (.a(Instruction[5:0]), .b(6'b010010), .eq(comparator_38_eq));  // open: gt, lt

  // Other names for the same wires on the sheet: Constante[15:0] = Instruction[15:0];
  //   Destino_salto[25:0] = Instruction[25:0]; FUNC_CODE[5:0] = Instruction[5:0]; x[4:0] = Instruction[10:6];
  //   Rd[4:0] = Instruction[15:11]; Rt[4:0] = Instruction[20:16]; Rs[4:0] = Instruction[25:21];
  //   OP_CODE[5:0] = Instruction[31:26]

  // Notes on the sheet:
  //   Instruction Decoder
  //   Output_Zone
endmodule

module Branch_Control (
  input  NOP,
  input  BEQ,
  input  [25:0] DEST,
  input  [31:0] RS,
  input  [31:0] RT,
  input  [31:0] PC,
  input  BNE,
  input  [15:0] OFFSET,
  input  BLEZ,
  input  BGTZ,
  input  BLTZ,
  input  JR,
  input  J,
  output [31:0] BC_OUT
);

  wire and_1_out, and_2_out, and_3_out, and_4_out, and_5_out, and_6_out, comparator_1_eq, not_1_out,
       or_1_out, RS__0, RS___0, RS____RT;
  wire [1:0] or_3_out;
  wire [31:0] PC_4, PC_4_4_OFFSET;
  wire [31:18] bit_extender_1_out;

  and and_1 (and_1_out, BEQ, RS____RT);
  and and_2 (and_2_out, ~RS____RT, BNE);  // AND_Gate
  and and_3 (and_3_out, BLEZ, RS___0);
  and and_4 (and_4_out, ~RS___0, BGTZ);  // AND_Gate
  and and_5 (and_5_out, BLTZ, RS__0);
  // Probe on {bit_extender_1_out, OFFSET, 2'b00}
  or or_1 (or_1_out, and_1_out, and_2_out, and_3_out, and_4_out, and_5_out);
  Adder #(.width(32)) adder_1 (.a(PC), .b(32'h4), .out(PC_4));  // open: cin, cout
  assign bit_extender_1_out = {{13{OFFSET[15]}}, OFFSET[15]};  // Bit_Extender bit_extender_1
  and and_6 (and_6_out, or_1_out, not_1_out);
  not not_1 (not_1_out, NOP);
  Adder #(.width(32)) adder_2 (
    .a(PC_4), .b({bit_extender_1_out, OFFSET, 2'b00}), .out(PC_4_4_OFFSET));  // open: cin, cout
  or or_2 (or_3_out[1], J, JR);
  or or_3 (or_3_out[0], and_6_out, JR);
  Comparator #(.width(32)) comparator_1 (.a(RS), .b({32{1'b0}}), .eq(comparator_1_eq), .lt(RS__0));  // open: gt
  Comparator #(.width(32)) comparator_2 (.a(RS), .b(RT), .eq(RS____RT));  // open: gt, lt
  // Probe on or_3_out
  or or_4 (RS___0, comparator_1_eq, RS__0);
  Multiplexer #(.select(2), .width(32), .enable("false")) multiplexer_1 (
    .in0(PC_4), .in1(PC_4_4_OFFSET), .in2({PC[31:28], DEST, 2'b00}), .in3(RS), .out(BC_OUT), .sel(or_3_out));
  // Probe on OFFSET

  // Other names for the same wires on the sheet: Jmp[31:2] = {PC[31:28], DEST}

  // Notes on the sheet:
  //   Branch Control
endmodule

module Program_Counter (
  input  [31:0] INPUT,
  input  RESET,
  input  ENABLE,
  input  CLK,
  output [31:0] PC_OUTPUT
);

  Register #(.width(32)) register_1 (.D(INPUT), .en(ENABLE), .Q(PC_OUTPUT), .clk(CLK), .clr(RESET));

  // Notes on the sheet:
  //   Program Counter
endmodule
